// Logisim project RRISC.circ as structural Verilog: 4 circuits, main circuit main
module main (
);

  wire ACC_OUT_IS_JUMP, ACC_OUT_IS_SKIP, and_1_out, BTN_out, CLK, d_ff_1_q, d_ff_1_qn, dipswitch_1_p1, EX,
       INST_MEM, INST_MEMWRITE, INSTF, not_1_out, RST, WB, WRITEFLAG;
  wire [0:0] not_2_out;
  wire [3:0] ACC_OUT_RX_WB;
  wire [7:0] ALU_OUT_RESULT, IR_q, MEMDATAIN, MEMDATAOUT, multiplexer_3_out, R0_ACC, R_CMP;
  wire [15:0] adder_1_out, MEM_PC, multiplexer_1_out, multiplexer_2_out, REGS_OUT_MEM;

  D_Flip_Flop d_ff_1 (.D(d_ff_1_qn), .clk(and_1_out), .Q(d_ff_1_q), .Qn(d_ff_1_qn));  // open: preset, reset
  LED led_1 (.in(d_ff_1_q));
  Multiplexer #(.enable("false"), .width(16)) multiplexer_1 (
    .in0(REGS_OUT_MEM), .in1(MEM_PC), .out(multiplexer_1_out), .sel(INSTF));
  RAM #(.addrWidth(16), .databus("bidir"), .trigger("high")) ram_1 (
    .addr(multiplexer_1_out), .we(and_1_out), .oe(not_1_out), .data(MEMDATAOUT));
  and and_1 (and_1_out, INST_MEMWRITE, INST_MEM, WRITEFLAG);
  not not_1 (not_1_out, and_1_out);
  Register #(.width(16)) PC (.D(multiplexer_2_out), .en(1'b1), .clk(WB), .Q(MEM_PC), .clr(RST));
  Multiplexer #(.enable("false"), .width(16)) multiplexer_2 (
    .in0(adder_1_out), .in1(REGS_OUT_MEM), .out(multiplexer_2_out), .sel(ACC_OUT_IS_JUMP));
  not not_2 (not_2_out[0], ACC_OUT_IS_SKIP);
  Adder #(.width(16)) adder_1 (
    .a(MEM_PC), .b({{14{1'b0}}, ACC_OUT_IS_SKIP, not_2_out[0]}), .out(adder_1_out));  // open: cin, cout
  assign MEMDATAOUT = and_1_out ? MEMDATAIN : 8'bz;  // Controlled_Buffer controlled_buffer_1
  // DipSwitch #(.number(2)) dipswitch_1: pin names not known; wires that end beside it: dipswitch_1_p1
  Button BTN (.out(BTN_out));
  Button BRST (.out(RST));
  Register IR (.D(MEMDATAOUT), .en(1'b1), .clk(EX), .Q({IR_q[7:5], INST_MEMWRITE, IR_q[3:0]}), .clr(RST));
  // Probe on MEMDATAOUT
  // Probe on {IR_q[7:5], INST_MEMWRITE, IR_q[3:0]}
  D_Flip_Flop #(.trigger("falling")) d_ff_2 (.D(EX), .clk(CLK), .Q(WRITEFLAG), .reset(RST));  // open: Qn, preset
  // Probe on multiplexer_3_out
  Multiplexer #(.enable("false"), .width(8)) multiplexer_3 (
    .in0(ALU_OUT_RESULT), .in1(MEMDATAOUT), .out(multiplexer_3_out), .sel(INST_MEM));
  // Probe on IR_q[3:0]
  // Probe on ACC_OUT_RX_WB
  Controller controller_1 (
    .STEP(dipswitch_1_p1), .BTN(BTN_out), .RST(RST), .INSTF(INSTF), .EX(EX), .WB(WB), .OUT_CLK(CLK));
  and u_INST_MEM (INST_MEM, IR_q[5], IR_q[6], IR_q[7]);
  // Probe on R0_ACC
  REGS regs_1 (
    .RST(RST), .Data(multiplexer_3_out), .CLK(WB), .Write(WRITEFLAG), .Rx_Read(IR_q[3:0]),
    .Rx_Write(ACC_OUT_RX_WB), .OUT_R0_ACC(R0_ACC), .OUT_REGDATA(MEMDATAIN), .OUT_CMP(R_CMP),
    .OUT_MEM(REGS_OUT_MEM));
  // Probe on ALU_OUT_RESULT
  ALU alu_1 (
    .IN_ACC(R0_ACC), .IN_CMP(R_CMP), .OPCODE({IR_q[7:5], INST_MEMWRITE}), .IN_IMMEDIATE(IR_q[3:0]),
    .REGDATA(MEMDATAIN), .IN_WB_FLAGS(WB), .IN_RST_FLAGS(RST), .OUT_RX_WB(ACC_OUT_RX_WB),
    .OUT_RESULT(ALU_OUT_RESULT), .OUT_IS_JUMP(ACC_OUT_IS_JUMP), .OUT_IS_SKIP(ACC_OUT_IS_SKIP));
  // Probe on R0_ACC
  // Probe on R_CMP
  // Probe on REGS_OUT_MEM
  // Probe on ALU_OUT_RESULT

  // Notes on the sheet:
  //   11ns
  //   40MHz = 25ns
  //   30MHz = 33.3ns
  //   20MHz = 50ns
  //   15MHz = 66.6ns
  //   10MHz = 100ns
  //   <- Expected 16MHz
  //   <- Test around 1kHz
  //   6ns
  //   Does  one cycle per press
  //   Every stage MUST effect state logic
  //   5ns 74as
  //   ~40ns
  //   12ns
  //   INST_ALU = !INST_MEM
  //   34:14
  //   Instf: Sets mem to PC. Data clocked into IR at end.
  //   EX: Spends cycle feeding-through ALU. Data clocked into WB at end.
  //   WE Pulled high for cycle. Writes to registers. Writes to memory if inst_memwrite
endmodule

module ALU (
  input  [7:0] IN_ACC,
  input  [7:0] IN_CMP,
  input  [3:0] OPCODE,
  input  [3:0] IN_IMMEDIATE,
  input  [7:0] REGDATA,
  input  IN_WB_FLAGS,
  input  IN_RST_FLAGS,
  output [3:0] OUT_RX_WB,
  output [7:0] OUT_RESULT,
  output OUT_IS_JUMP,
  output OUT_IS_SKIP
);

  wire and_1_out, and_2_out, comparator_1_eq, comparator_1_gt, comparator_1_lt, FLAG_CARRY_IN,
       FLAG_CARRY_OUT, multiplexer_5_out, nor_1_out, not_1_out, not_2_out, or_1_out, xor_1_out;
  wire [7:0] adder_1_out, and_5_out, bit_extender_1_out, multiplexer_6_out, multiplexer_7_out,
       multiplexer_8_out, multiplexer_9_out, or_2_out, REG_OR_ONESIMM, xor_2_out, xor_3_out;
  wire [7:4] REG_OR_ZEROIMM;

  Comparator comparator_1 (.a(IN_ACC), .b(IN_CMP), .gt(comparator_1_gt), .eq(comparator_1_eq), .lt(comparator_1_lt));
  Multiplexer #(.enable("false"), .width(4)) multiplexer_1 (
    .in0(4'b0000), .in1(IN_IMMEDIATE), .out(OUT_RX_WB), .sel(and_1_out));
  and and_1 (and_1_out, OPCODE[0], OPCODE[1], OPCODE[2]);
  or or_1 (or_1_out, IN_ACC[0], IN_ACC[1], IN_ACC[2], IN_ACC[3], IN_ACC[4], IN_ACC[5], IN_ACC[6], IN_ACC[7]);
  Multiplexer #(.enable("false"), .width(4)) multiplexer_2 (
    .in0(4'b1111), .in1(REGDATA[7:4]), .out(REG_OR_ONESIMM[7:4]), .sel(OPCODE[0]));
  Multiplexer #(.enable("false"), .width(4)) multiplexer_3 (
    .in0(4'b0000), .in1(REGDATA[7:4]), .out(REG_OR_ZEROIMM), .sel(OPCODE[0]));
  Multiplexer #(.enable("false"), .width(4)) multiplexer_4 (
    .in0(IN_IMMEDIATE), .in1(REGDATA[3:0]), .out(REG_OR_ONESIMM[3:0]), .sel(OPCODE[0]));
  Multiplexer #(.enable("false"), .select(3)) multiplexer_5 (
    .in0(1'b1), .in1(or_1_out), .in2(IN_ACC[7]), .in3(comparator_1_lt), .in4(comparator_1_eq),
    .in5(comparator_1_gt), .in6(IN_ACC[0]), .in7(FLAG_CARRY_OUT), .out(multiplexer_5_out),
    .sel(IN_IMMEDIATE[3:1]));
  xor xor_1 (xor_1_out, multiplexer_5_out, IN_IMMEDIATE[0]);
  not not_1 (not_1_out, OPCODE[1]);
  and and_2 (and_2_out, OPCODE[3], OPCODE[2], not_1_out, xor_1_out);
  assign bit_extender_1_out = {{7{OPCODE[1]}}, OPCODE[1]};  // Bit_Extender bit_extender_1
  not not_2 (not_2_out, OPCODE[0]);
  assign xor_2_out = {REG_OR_ZEROIMM, REG_OR_ONESIMM[3:0]} ^ bit_extender_1_out;  // XOR_Gate xor_2, 8 bits wide
  and and_3 (OUT_IS_JUMP, and_2_out, OPCODE[0]);
  and and_4 (OUT_IS_SKIP, and_2_out, not_2_out);
  Adder adder_1 (.a(IN_ACC), .b(xor_2_out), .out(adder_1_out), .cin(OPCODE[1]), .cout(FLAG_CARRY_IN));
  assign and_5_out = IN_ACC & REG_OR_ONESIMM;  // AND_Gate and_5, 8 bits wide
  Multiplexer #(.enable("false"), .width(8)) multiplexer_6 (
    .in0(REGDATA), .in1(IN_ACC), .out(multiplexer_6_out), .sel(OPCODE[0]));
  assign or_2_out = IN_ACC | {REG_OR_ZEROIMM, REG_OR_ONESIMM[3:0]};  // OR_Gate or_2, 8 bits wide
  assign xor_3_out = IN_ACC ^ {REG_OR_ZEROIMM, REG_OR_ONESIMM[3:0]};  // XOR_Gate xor_3, 8 bits wide
  nor nor_1 (nor_1_out, OPCODE[3], OPCODE[2]);
  Register #(.width(1)) FLAG_CARRY (
    .D(FLAG_CARRY_IN), .en(nor_1_out), .clk(IN_WB_FLAGS), .Q(FLAG_CARRY_OUT), .clr(IN_RST_FLAGS));
  Multiplexer #(.enable("false"), .width(8)) multiplexer_7 (
    .in0({and_5_out[3:0], and_5_out[7:4]}), .in1(and_5_out), .out(multiplexer_7_out), .sel(OPCODE[0]));
  Multiplexer #(.enable("false"), .width(8)) multiplexer_8 (
    .in0({or_2_out[3:0], or_2_out[7:4]}), .in1(or_2_out), .out(multiplexer_8_out), .sel(OPCODE[0]));
  Multiplexer #(.enable("false"), .width(8)) multiplexer_9 (
    .in0({xor_3_out[3:0], xor_3_out[7:4]}), .in1(xor_3_out), .out(multiplexer_9_out), .sel(OPCODE[0]));
  Multiplexer #(.enable("false"), .select(3), .width(8)) multiplexer_10 (
    .in0(adder_1_out), .in1(adder_1_out), .in2(multiplexer_7_out), .in3(multiplexer_6_out),
    .in4(multiplexer_8_out), .in5(multiplexer_9_out), .in6(IN_ACC), .in7(IN_ACC), .out(OUT_RESULT),
    .sel(OPCODE[3:1]));

  // Other names for the same wires on the sheet: IMMEDIATE[3:0] = IN_IMMEDIATE; OPCODE_LSB = OPCODE[0];
  //   OPCODE_BIT1 = OPCODE[1]; REG_OR_ZEROIMM[3:0] = REG_OR_ONESIMM[3:0]

  // Notes on the sheet:
  //   If set or RB instruction: (DST=IMM) ELSE (DST=ACC)
  //   ROI [3:0]
  //   Data is register or immediate. The 4MSB of imm are 1s for ADD,OR and 0s for xor,add
  //   Conditional Jump
  //   Branch Event
  //   Branch event and instruction
  //   WE = add/sub = opcode 0-3
  //   ~40ns
  //   The actual ALU
  //   18.5ns
  //   Chip count: 30
  //   11ns
  //   Actual ALU Stuff
  //   ~40ns
endmodule

module REGS (
  input  RST,
  input  [7:0] Data,
  input  CLK,
  input  Write,
  input  [3:0] Rx_Read,
  input  [3:0] Rx_Write,
  output [7:0] OUT_R0_ACC,
  output [7:0] OUT_REGDATA,
  output [7:0] OUT_CMP,
  output [15:0] OUT_MEM
);

  wire demultiplexer_1_out0, demultiplexer_1_out1, demultiplexer_1_out2, demultiplexer_1_out3,
       demultiplexer_1_out4, demultiplexer_1_out5, demultiplexer_1_out6, demultiplexer_1_out7,
       demultiplexer_1_out8, demultiplexer_1_out9, demultiplexer_1_out10, demultiplexer_1_out11,
       demultiplexer_1_out12, demultiplexer_1_out13, demultiplexer_1_out14, demultiplexer_1_out15;
  wire [7:0] R1_q, R2_q, R3_q, R4_q, R5_q, R6_q, R7_q, R8_q, R9_q, R10_RAT_q, R12_RSH_q, R13_RSL_q;

  Demultiplexer #(.enable("false"), .select(4)) demultiplexer_1 (
    .out0(demultiplexer_1_out0), .out1(demultiplexer_1_out1), .out2(demultiplexer_1_out2),
    .out3(demultiplexer_1_out3), .out4(demultiplexer_1_out4), .out5(demultiplexer_1_out5),
    .out6(demultiplexer_1_out6), .out7(demultiplexer_1_out7), .out8(demultiplexer_1_out8),
    .out9(demultiplexer_1_out9), .out10(demultiplexer_1_out10), .out11(demultiplexer_1_out11),
    .out12(demultiplexer_1_out12), .out13(demultiplexer_1_out13), .out14(demultiplexer_1_out14),
    .out15(demultiplexer_1_out15), .in(Write), .sel(Rx_Write));
  Register R0_ACC (.D(Data), .en(demultiplexer_1_out0), .clk(CLK), .Q(OUT_R0_ACC), .clr(RST));
  Register R1 (.D(Data), .en(demultiplexer_1_out1), .clk(CLK), .Q(R1_q), .clr(RST));
  Register R2 (.D(Data), .en(demultiplexer_1_out2), .clk(CLK), .Q(R2_q), .clr(RST));
  Register R3 (.D(Data), .en(demultiplexer_1_out3), .clk(CLK), .Q(R3_q), .clr(RST));
  Register R4 (.D(Data), .en(demultiplexer_1_out4), .clk(CLK), .Q(R4_q), .clr(RST));
  Register R5 (.D(Data), .en(demultiplexer_1_out5), .clk(CLK), .Q(R5_q), .clr(RST));
  Register R6 (.D(Data), .en(demultiplexer_1_out6), .clk(CLK), .Q(R6_q), .clr(RST));
  Register R7 (.D(Data), .en(demultiplexer_1_out7), .clk(CLK), .Q(R7_q), .clr(RST));
  Register R8 (.D(Data), .en(demultiplexer_1_out8), .clk(CLK), .Q(R8_q), .clr(RST));
  Register R9 (.D(Data), .en(demultiplexer_1_out9), .clk(CLK), .Q(R9_q), .clr(RST));
  Register R10_RAT (.D(Data), .en(demultiplexer_1_out10), .clk(CLK), .Q(R10_RAT_q), .clr(RST));
  Register R11_CMP (.D(Data), .en(demultiplexer_1_out11), .clk(CLK), .Q(OUT_CMP), .clr(RST));
  Register R12_RSH (.D(Data), .en(demultiplexer_1_out12), .clk(CLK), .Q(R12_RSH_q), .clr(RST));
  Register R13_RSL (.D(Data), .en(demultiplexer_1_out13), .clk(CLK), .Q(R13_RSL_q), .clr(RST));
  Register R14_RMH (.D(Data), .en(demultiplexer_1_out14), .clk(CLK), .Q(OUT_MEM[15:8]), .clr(RST));
  Register R15_RML (.D(Data), .en(demultiplexer_1_out15), .clk(CLK), .Q(OUT_MEM[7:0]), .clr(RST));
  Multiplexer #(.enable("false"), .select(4), .width(8)) multiplexer_1 (
    .in0(OUT_R0_ACC), .in1(R1_q), .in2(R2_q), .in3(R3_q), .in4(R4_q), .in5(R5_q), .in6(R6_q), .in7(R7_q),
    .in8(R8_q), .in9(R9_q), .in10(R10_RAT_q), .in11(OUT_CMP), .in12(R12_RSH_q), .in13(R13_RSL_q),
    .in14(OUT_MEM[15:8]), .in15(OUT_MEM[7:0]), .out(OUT_REGDATA), .sel(Rx_Read));

  // Notes on the sheet:
  //   6ns
  //   6ns
  //   Is actually 8 16:1 muxes
endmodule

module Controller (
  input  STEP,
  input  BTN,
  input  RST,
  output INSTF,
  output EX,
  output WB,
  output OUT_CLK
);

  wire and_1_out, clock_1_out, demultiplexer_1_out3, or_1_out, or_2_out;
  wire [2:0] adder_1_out, CTR_q;

  or or_1 (or_1_out, ~INSTF, BTN);  // OR_Gate
  or or_2 (or_2_out, RST, demultiplexer_1_out3);
  Clock clock_1 (.out(clock_1_out));
  or or_3 (OUT_CLK, and_1_out, BTN);
  and and_1 (and_1_out, clock_1_out, or_1_out, STEP);
  Register #(.width(3)) CTR (.D(adder_1_out), .en(1'b1), .clk(OUT_CLK), .Q(CTR_q), .clr(or_2_out));
  Demultiplexer #(.enable("false"), .select(3)) demultiplexer_1 (
    .out0(INSTF), .out1(EX), .out2(WB), .out3(demultiplexer_1_out3), .in(1'b1), .sel(CTR_q));  // open: out4, out5, out6, out7
  Adder #(.width(3)) adder_1 (.a(CTR_q), .b(3'b001), .out(adder_1_out));  // open: cin, cout

  // Notes on the sheet:
  //   This is mostly just a ring counter for the pipeline
endmodule
